# Fritzing sketch ESP32_Shutter_Tester_3_0_9_0_minimal_schematic (saved by Fritzing 0.9.3b)

parts:
  Mod2 = KY-008 Laser Transmitter Module [package="Breakout board"]
  Mod3 = KY-008 Laser Transmitter Module [package="Breakout board"]  # not connected
  Mod4 = laser receiver [package=THT]
  Mod5 = laser receiver [package=THT]
  S1 = Round Pushbutton
  S2 = Round Pushbutton
  Part1 = node32s
  Mod6 = KY-008 Laser Transmitter Module [package="Breakout board"]
  Mod7 = laser receiver [package=THT]
  S3 = Round Pushbutton
  S4 = Round Pushbutton
  J1 = Basic Force Sensing Resistor (FSR) [package=THT]

nets:
  N1: Mod2.S, Mod4.pin3, Part1.3.3V
  N2: Mod2.-, Part1.V_BATT
  N3: Mod4.pin2, Part1.IO33
  N4: Mod5.pin2, Part1.IO32
  N5: S1.leg1, Part1.IO26
  N6: S2.leg0, Part1.IO27
  N7: Part1.IO25, Mod7.pin2
  N8: Part1.IO14, S4.leg0
  N9: Part1.IO12, S3.leg0
  N10: Part1.IO13, J1.pin_1
  N11: Mod6.S, Mod6.NC

notes:
  Caution
  To avoid sensor damage, wire up the rx modules BEFORE plugging the transparent senors into them. Double check wiring BEFORE powering up the board & ensure LEDs light.
  Then de-power the board and insert sensors ENSURING the sensor is fitted the correct way round.
  Transparent three legged sensors must be fitted with the flat surface at the rear and the little dome pointing overthe board and towards the laser.
  Connecting them incorrectly WILL destroy them.
  Note:-
  DO NOT use the GND pin on the EPS32 board, that is located between pins 19 & 21.
  1 2 3 4
  V3.16 minimal
  Smallest design that will work.
  V3.17
  Laser pins &
  Button wire colours
  harmonised.
  Optional
  Flash plug.
  Centre pin -Green
  Outer - Black

custom parts:
  KY-008 Laser Transmitter Module: KY-008 Laser Transmitter Module, emits a dot shaped red laser beam.
  laser receiver: Generic non modulated laser receiver module.
