# Fritzing sketch ESP32_Shutter_Tester tft_4_0_0_0_Full (saved by Fritzing 0.9.3b)

parts:
  Mod2 = KY-008 Laser Transmitter Module [package="Breakout board"]  # not connected
  Mod3 = KY-008 Laser Transmitter Module [package="Breakout board"]  # not connected
  Mod4 = laser receiver [package=THT]
  Mod5 = laser receiver [package=THT]
  S1 = Round Pushbutton
  S2 = Round Pushbutton
  Part1 = node32s
  Mod6 = KY-008 Laser Transmitter Module [package="Breakout board"]
  Mod7 = laser receiver [package=THT]
  S3 = Round Pushbutton
  S4 = Round Pushbutton
  LCD1 = 2.8" SPI TFT Module [part_number=MSP2807]
  J1 = Basic Force Sensing Resistor (FSR) [package=THT]
  S5 = Round Pushbutton
  8x8_LED_Modul_mit_MAX1 = 8x8 LED Modul mit MAX7219 [package=THT]
  LCD2004-I2C4 = LCD2004-I2C
  RE2 = Rotary Encoder [package=THT]  # not connected
  Part3 = BH1750

nets:
  N1: Mod4.pin1, Part1.V_BATT, J1.pin_0, S5.leg1
  N2: Mod4.pin2, Part1.IO33
  N3: Mod5.pin2, Part1.IO32
  N4: S1.leg0, Part1.IO26
  N5: S2.leg0, Part1.IO27
  N6: Part1.3.3V, LCD1.pin1
  N7: Part1.IO25, Mod7.pin2
  N8: Part1.IO14, S4.leg0
  N9: Part1.IO12, S3.leg0
  N10: Part1.IO13, J1.pin_1
  VCC: Part1.5V, 8x8_LED_Modul_mit_MAX1.VCC_Eingang, LCD2004-I2C4.VCC, Part3.VCC
  GND: Part1.GND, LCD1.pin2, 8x8_LED_Modul_mit_MAX1.GND_Eingang, LCD2004-I2C4.GND, Part3.GND
  N11: Part1.IO23, LCD1.pin6, 8x8_LED_Modul_mit_MAX1.DIN_Eingang
  N12: Part1.IO22, LCD2004-I2C4.SCL, Part3.SCL
  N13: Part1.IO21, LCD2004-I2C4.SDA, Part3.SDA
  N14: Part1.IO18, LCD1.pin7, 8x8_LED_Modul_mit_MAX1.CLK_Eingang
  N15: Part1.IO5, LCD1.pin3
  N16: Part1.IO16, LCD1.pin5
  N17: Part1.IO4, LCD1.pin4
  N18: Part1.IO0, S5.leg0
  N19: Part1.IO15, 8x8_LED_Modul_mit_MAX1.CS_Eingang
  N20: Mod6.S, Mod6.NC

notes:
  Caution
  To avoid sensor damage, wire up the rx modules BEFORE plugging the transparent senors into them. Double check wiring BEFORE powering up the board & ensure LEDs light.
  Then de-power the board and insert sensors ENSURING the sensor is fitted the correct way round.
  Mandatory (JST)
  4" / 3.95" SPI TFT
  ILI9488 Driver
  480 X 320
  Transparent three legged sensors must be fitted with the flat surface at the rear and the little dome pointing over the board and towards the laser.
  Connecting them incorrectly WILL destroy them.
  TFT pins in order ESP32 Wire Colour
  TFT_VDD 3V3 Red
  TFT_GND GND Black
  TFT_CS 5 White Chip select
  TFT_RST 4 Yellow Reset pin
  TFT_DC 16 (2) Orange Data Command
  TFT_MOSI 23 Green
  TFT_SCLK 18 Blue
  TFT_LED 3V3 Purple
  TFT_MISO ----- do no connect
  Wiring below not required
  Touch_CCLK 18 Blue
  Touch_CS 2 (15) Orange
  Touch_DIN 23 Green MOSI
  Touch_TFT_DO 19 Violet MISO
  Touch_IRQ do not connect
  Note:-
  DO NOT use the GND pin on the EPS32 board, that is located between pins 19 & 21.
  1 2 3 4 5
  White Yellow Green Black Red
  Display Ave Ave-Reset LightMeter Menu LED Matrix
  Version 4.0.0.2
  ********************
  Optional
  Flash plug.
  Centre pin -Green
  Outer - Black
  Optional
  Light Sensor (JST)
  GY-302
  module
  (5V)
  Optional
  LED Matrix (JST)
  (shown upside down)
  (5V)
  Optional LCD - Depreciated.
  Connections to iic on rear of LCD
  Black GND
  Red VCC (5V)
  Orange SDA - 21
  Yellow SCL - 22
  Encoder - (JST)
  Red - 3.3V
  Orange - Btn
  White - S2
  Yellow - S1
  Black - GND
  Caution:-
  Both 3.3Volt and 5 Volt devices are used.
  3.3V wires are shown in Brown
  5V wires are shown in Red.
  When using JST connectors, there is no Brown wire, so use Red but be very careul to ensure correct connections.
  Notes on wiring Colours
  3.3V are shown in Brown, and 5V are shown in Red, for clarity.
  As the JST HX connectors do not contain a Red wire, use Red for both 3.3 & 5V wires, but use extreme caution.
  The wiring and photos of this Shutter Tester build used pre-made JST HX connectors, which contain an Orange wire.(which require the ins removed and swaped in the housing)
  The cheap Aliexpress JST HX kits do not contain an Orange wire.
  It is suggested that Blue is used an an altenate colour.

custom parts:
  KY-008 Laser Transmitter Module: KY-008 Laser Transmitter Module, emits a dot shaped red laser beam.
  laser receiver: Generic non modulated laser receiver module.
  2.8" SPI TFT Module: A generic 2.8 inch LCD TFT 320x240 display with touchscreen and SD card slot. Uses the ILI9341 controller, like the Adafruit displays of this size uses.
  LCD2004-I2C: A standard character display with 4x20 characters. Comes in many colors with LCM2004 IIC attached.
  BH1750: Light Sensor
