# Fritzing sketch ESP32_Shutter_Tester tft_4_0_1_1_full (saved by Fritzing 0.9.3b)

parts:
  Mod2 = KY-008 Laser Transmitter Module [package="Breakout board"]  # not connected
  Mod3 = KY-008 Laser Transmitter Module [package="Breakout board"]  # not connected
  Mod4 = laser receiver [package=THT]
  Mod5 = laser receiver [package=THT]
  S1 = Round Pushbutton
  S2 = Round Pushbutton
  Part1 = node32s
  Mod6 = KY-008 Laser Transmitter Module [package="Breakout board"]
  Mod7 = laser receiver [package=THT]
  S3 = Round Pushbutton
  S4 = Round Pushbutton
  LCD1 = 2.8" SPI TFT Module [part_number=MSP2807]
  J1 = Basic Force Sensing Resistor (FSR) [package=THT]
  S5 = Round Pushbutton
  8x8_LED_Modul_mit_MAX1 = 8x8 LED Modul mit MAX7219 [package=THT]
  LCD2004-I2C4 = LCD2004-I2C  # not connected
  RE2 = Rotary Encoder [package=THT]  # not connected
  Part3 = BH1750

nets:
  N1: Mod4.pin2, Part1.IO33
  N2: Mod5.pin2, Part1.IO32
  N3: S1.leg0, Part1.IO26
  N4: S2.leg0, Part1.IO27
  N5: Part1.3.3V, LCD1.pin1
  N6: Part1.IO25, Mod7.pin2
  N7: Part1.IO14, S4.leg0
  N8: Part1.IO12, S3.leg0
  N9: Part1.V_BATT, J1.pin_1
  5V: Part1.5V, 8x8_LED_Modul_mit_MAX1.VCC_Eingang, Part3.VCC
  GND: Part1.GND, LCD1.pin2, 8x8_LED_Modul_mit_MAX1.GND_Eingang, Part3.GND
  N10: Part1.IO23, LCD1.pin6, LCD1.pin12, 8x8_LED_Modul_mit_MAX1.DIN_Eingang
  N11: Part1.IO22, Part3.SCL
  N12: Part1.IO21, Part3.SDA
  N13: Part1.IO19, LCD1.pin13
  N14: Part1.IO18, LCD1.pin7, LCD1.pin10, 8x8_LED_Modul_mit_MAX1.CLK_Eingang
  N15: Part1.IO5, LCD1.pin3
  N16: Part1.IO16, LCD1.pin5
  N17: Part1.IO4, LCD1.pin4
  N18: Part1.IO0, S5.leg0
  N19: Part1.IO2, LCD1.pin11
  N20: Part1.IO15, 8x8_LED_Modul_mit_MAX1.CS_Eingang
  N21: Mod6.S, Mod6.NC

notes:
  Caution
  To avoid sensor damage, wire up the rx modules BEFORE plugging the transparent senors into them. Double check wiring BEFORE powering up the board & ensure LEDs light.
  Then de-power the board and insert sensors ENSURING the sensor is fitted the correct way round.
  Mandatory (JST)
  4" / 3.95" SPI TFT
  ILI9488 Driver
  480 X 320
  Transparent three legged sensors must be fitted with the flat surface at the rear and the little dome pointing over the board and towards the laser.
  Connecting them incorrectly WILL destroy them.
  TFT pins in order ESP32 Wire Colour
  TFT_VDD 3V3 Red
  TFT_GND GND Black
  TFT_CS 5 White Chip select
  TFT_RST 4 Yellow Reset pin
  TFT_DC 16 (2) Blue Data Command
  TFT_MOSI 23 Green
  TFT_SCLK 18 Blue
  TFT_LED 3V3 Brown
  TFT_MISO ----- do no connect
  Optional Touch Wiring
  Touch_CCLK 18 Blue
  Touch_CS 2 (15) White
  Touch_DIN 23 Green MOSI
  Touch_TFT_DO 19 Yellow MISO
  Touch_IRQ do not connect
  Optional Sd Card conections for dataLogger
  CLK (SLK) 18 Blue
  SDO (MISO) 19 Yellow
  SDI (MOSI) 23 Green
  SCS (CS) 17 White
  Note:-
  DO NOT use the GND pin on the EPS32 board, that is located between pins 19 & 21.
  1 2 3 4 5
  White Yellow Green Black Red
  Pin 26 Pin 27 Pin 14 Pin 12 Pin 0
  Display Ave Ave-Reset LightMeter Menu LED Matrix
  Version 4.0.1.1
  December 2025
  ********************
  wiring for SD card added
  wiring foTFT touch added
  Orange wires changed to blue for compatibility with connector kit.
  Optional Flash plug.
  Conn. ESP32 Colour
  Centre pin 13 Green
  Outer - GND Black
  OptionalLight SensorGY-302
  module ESP32 Pin Wire Colour
  ADDR - GND Black
  SDA 21 White
  SCL 22 Yellow
  GND GND Black
  VCC 5V Red
  Optional LED Matrix
  LED ESP32 Pin Wire Colour
  Vcc 5V Red
  GND 0V Black
  DIN 23 Green
  CS 15 White
  Optional LCD - Depreciated. Connections to iic on rear of LCD
  LCD ESP32 Pin Wire Colour
  0V GND Black
  VCC 5V Red
  SDA 21 White
  SCL 22 Yellow
  Encoder
  Encoder ESp32 Pin Wire Colour
  3.3V 3V3 Red
  Key 34 Blue
  S2 36 White
  S1 39 Yellow
  0V GND Black
  Caution:-
  Both 3.3 Volt and 5 Volt devices are used.
  3.3V wires are shown in Brown
  5V wires are shown in Red.
  When using JST connectors, there is no Brown wire, so use Red (or order seperate brown wires) but be very careul to ensure correct connections.
  Sensors
  Sensor Out EPS32 Pin Wire Colour
  sen3 33 Yellow
  senM 25 Green
  Sen1 32 Blue
  GND GND Black
  VCC 3V3 Brown
  Optional wiring for SD card
  17/23/19/18
  Caution on TFT Wiring.
  Connector is on the rear of the TFT.
  Ensure you do not wire up as a mirror image.
  Caution
  TFT is powered by 3V3
  Ensure you correctly wire the TFT.

custom parts:
  KY-008 Laser Transmitter Module: KY-008 Laser Transmitter Module, emits a dot shaped red laser beam.
  laser receiver: Generic non modulated laser receiver module.
  2.8" SPI TFT Module: A generic 2.8 inch LCD TFT 320x240 display with touchscreen and SD card slot. Uses the ILI9341 controller, like the Adafruit displays of this size uses.
  LCD2004-I2C: A standard character display with 4x20 characters. Comes in many colors with LCM2004 IIC attached.
  BH1750: Light Sensor
